# Fritzing sketch boardGroundFilled (saved by Fritzing 0.9.3b)
circuit board: 9.04594cm x 7.1307cm
breadboards: 1

parts:
  U1 = ESP32-38PinWide [part_number=ESP32-38PinWide]
  Food_Scale_HX711 = HX711 Weighing Sensor Module
  Conv_5V = IC, SIP package, 3 pins [chip_label=->5V]
  CPOWER = SIP - 2 pins [chip_label=IC package="SIP (Single Inline) [THT]"]
  C_FoodScale = IC, SIP package, 4 pins [chip_label=JST]
  C_Cat = IC, SIP package, 5 pins [chip_label=JST]
  C_Buzzer = IC, SIP package, 3 pins [chip_label=Buzzer]
  J_BuzzVcc = IC, SIP package, 3 pins [chip_label="JMP Buzz"]
  C_SD_CARD = IC, SIP package, 7 pins [chip_label=JMC]
  R1 = Resistor [tolerance=±5% resistance=22k package=THT]
  R2 = Resistor [tolerance=±5% resistance=22k package=THT]
  R3 = Resistor [tolerance=±5% resistance=22k package=THT]
  R4 = Resistor [tolerance=±5% resistance=22k package=THT]
  JV1 = female pin header, 3 pins [form="♀ (female)"]
  JV2 = female pin header, 3 pins [form="♀ (female)"]
  R7 = Resistor [tolerance=±5% resistance=47k package=THT]
  R8 = Resistor [tolerance=±5% resistance=4.7k package=THT]
  JV3 = female pin header, 3 pins [form="♀ (female)"]
  C_Hall_1 = IC, SIP package, 3 pins [chip_label="A3141 JST"]
  C_Hall_2 = IC, SIP package, 3 pins [chip_label="A3141 JST"]
  R9 = Resistor [tolerance=±5% resistance=51k package=THT]
  R10 = Resistor [tolerance=±5% resistance=51k package=THT]
  C1 = Ceramic Capacitor [capacitance=100nF package="100 mil [THT, multilayer]"]
  C2 = Ceramic Capacitor [capacitance=100nF package="100 mil [THT, multilayer]"]
  C_LED_Strip = IC, SIP package, 3 pins [chip_label=JMC]
  R11 = Resistor [tolerance=±5% resistance=470 package=THT]
  C3 = Tantalum Capacitor [capacitance=999µF voltage=25V package="200 mil [THT, tantalum]"]
  C4 = Tantalum Capacitor [capacitance=999µF voltage=25V package="200 mil [THT, tantalum]"]
  C5 = Tantalum Capacitor [capacitance=999µF voltage=25V package="200 mil [THT, tantalum]"]
  C6 = Tantalum Capacitor [capacitance=999µF voltage=25V package="200 mil [THT, tantalum]"]
  IC1 = ULN2003A [package="DIP16 [THT]"]
  C7 = Ceramic Capacitor [capacitance=100nF package="100 mil [THT, multilayer]"]
  C_Lid_Motor = IC, SIP package, 5 pins [chip_label=JMC]
  Pololu_A1 = Pololu A4988 [package=SO16]
  C8 = Ceramic Capacitor [capacitance=100nF package="100 mil [THT, multilayer]"]
  C_FMotor = IC, SIP package, 4 pins [chip_label=JST]
  JMSx = double row female pin header, 6 pins [form="♀ (female)"]
  JFoodCh = double row rounded female pin header, 8 pins [form="♀ (female rounded)"]

nets:
  3.3V: U1.3.3, Food_Scale_HX711.VCC, C_Cat.pin2, J_BuzzVcc.pin3, C_SD_CARD.pin4, JV1.pin3, JV2.pin3, C_Hall_1.pin1, C_Hall_2.pin1, R9.Pin_0, R10.Pin_0, C6.+, Pololu_A1.RESET, Pololu_A1.SLEEP, Pololu_A1.VDD, C8.1, JMSx.pin4, JMSx.pin5, JMSx.pin6
  N1: U1.GPIO36, C_Hall_1.pin3, R9.Pin_1, C1.1
  N2: U1.GPIO39, C_Hall_2.pin3, R10.Pin_1, C2.1
  N3: U1.GPIO34, R1.Pin_0, R2.Pin_1
  N4: U1.GPIO35, R3.Pin_0, R4.Pin_1
  N5: U1.GPIO32, R7.Pin_0, R8.Pin_1
  N6: U1.GPIO33, C_Cat.pin1
  N7: U1.GPIO25, C_Cat.pin4
  N8: U1.GPIO26, C_Cat.pin5
  N9: U1.GPIO14, Pololu_A1.STEP
  N10: U1.GPIO12, Pololu_A1.DIR
  GND: U1.GND, Food_Scale_HX711.GND, Conv_5V.pin2, CPOWER.pin2, C_Cat.pin3, C_Buzzer.pin1, C_SD_CARD.pin3, C_SD_CARD.pin6, R2.Pin_0, R4.Pin_0, R8.Pin_0, C_Hall_1.pin2, C_Hall_2.pin2, C1.0, C2.0, C_LED_Strip.pin3, C3.-, C4.-, C5.-, C6.-, IC1.In_5, IC1.In_6, IC1.In_7, IC1.0V, C7.0, Pololu_A1.GND, C8.0
  N11: U1.GPIO13, Pololu_A1.ENABLE
  5V: U1.VIN, Conv_5V.pin1, J_BuzzVcc.pin1, JV1.pin1, JV2.pin1, JV3.pin1, C_LED_Strip.pin1, C3.+, C5.+, IC1.COM_-_Common, C7.1, C_Lid_Motor.pin5
  N12: U1.GPIO15, IC1.In_4
  N13: U1.GPIO2, IC1.In_3
  N14: U1.GPIO0, IC1.In_2
  N15: U1.GPIO4, IC1.In_1
  N16: U1.GPIO16, Food_Scale_HX711.CK/TX
  N17: U1.GPIO17, Food_Scale_HX711.DO/RX
  N18: U1.GPIO5, C_SD_CARD.pin1
  N19: U1.GPIO18, C_SD_CARD.pin5
  N20: U1.GPIO19, C_SD_CARD.pin7
  N21: U1.GPIO21, C_Buzzer.pin2
  N22: U1.GPIO22, R11.Pin_0
  N23: U1.GPIO23, C_SD_CARD.pin2
  N24: Food_Scale_HX711.E+, C_FoodScale.pin3
  N25: Food_Scale_HX711.E-, C_FoodScale.pin4
  N26: Food_Scale_HX711.A+, JFoodCh.pin1
  N27: Food_Scale_HX711.A-, JFoodCh.pin3
  N28: Food_Scale_HX711.B+, JFoodCh.pin2
  N29: Food_Scale_HX711.B-, JFoodCh.pin4
  N30: Conv_5V.pin3, CPOWER.pin1, JV3.pin3, C4.+, Pololu_A1.VMOT
  N31: C_FoodScale.pin1, JFoodCh.pin5, JFoodCh.pin6
  N32: C_FoodScale.pin2, JFoodCh.pin7, JFoodCh.pin8
  N33: C_Buzzer.pin3, J_BuzzVcc.pin2
  N34: R1.Pin_1, JV2.pin2
  N35: R3.Pin_1, JV1.pin2
  N36: R7.Pin_1, JV3.pin2
  N37: C_LED_Strip.pin2, R11.Pin_1
  N38: IC1.Out_4, C_Lid_Motor.pin4
  N39: IC1.Out_3, C_Lid_Motor.pin3
  N40: IC1.Out_2, C_Lid_Motor.pin2
  N41: IC1.Out_1, C_Lid_Motor.pin1
  N42: Pololu_A1.MS1, JMSx.pin1
  N43: Pololu_A1.MS2, JMSx.pin2
  N44: Pololu_A1.MS3, JMSx.pin3
  N45: Pololu_A1.1B, C_FMotor.pin4
  N46: Pololu_A1.1A, C_FMotor.pin3
  N47: Pololu_A1.2A, C_FMotor.pin2
  N48: Pololu_A1.2B, C_FMotor.pin1

notes:
  Karmniczun Emmy v1

custom parts:
  ESP32-38PinWide: Generic 38-Pin ESP32 with wide format (only access to one side of pins on a breadboard) based on Stephen Lilley's HiLetgo ESP-WROOM-32 ESP32 ESP-32S Development Board.
